# Fritzing sketch SchaltplanFenster (saved by Fritzing 1.0.5)
breadboards: 1

parts:
  esp1 = ESP32 DevKitc V4
  MH-Z19C1 = MH-Z19C  # not connected
  DHT1 = DHT22 Humidity and Temperature Sensor
  M1 = Stepper Motor - Bipolar  # not connected
  U1 = A3144 Hall Effect Sensor. [package="UA [THT]"]
  M2 = Stepper Motor - Bipolar  # not connected
  S1 = Round Pushbutton  # not connected
  R1 = Resistor [tolerance=±5% resistance=10k package="0402 [SMD]"]  # not connected
  C1 = Tantalum Capacitor [capacitance=100nF voltage=35V package="200 mil [THT, tantalum]"]
  VCC1 = 4 x AAA Battery Mount [internal_resistance=0.1Ω]

nets:
  N1: esp1.IO19, U1.Out
  N2: esp1.IO21, DHT1.DATA
  GND: esp1.GND, DHT1.GND, U1.GND, C1.-, VCC1.-
  5V: esp1.5V, DHT1.VDD, U1.+Vsupply, C1.+, VCC1.+

custom parts:
  ESP32 DevKitc V4: ESP32-DevKitC board with ESP32-WROOM-32 module. ESP32-DevKitC V4 is a small-sized ESP32-based development board produced by Espressif. Most of the pins on the ESP module are broken out to the pin headers on the board. The pins D0, D1, D2, D3, CMD and CLK are used internally for communication between ESP32 and SPI flash memory. They are grouped on both sides near the USB connector. Avoid using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
  MH-Z19C: CO2-Sensor https://www.winsen-sensor.com/
  A3144 Hall Effect Sensor.: Allegro A3144 hall effect switch for high temperature operation.
